# Fritzing sketch wiring (saved by Fritzing 0.9.4)
breadboards: 2

parts:
  Part1 = Arduino Uno (Rev3)
  ESP8266 = ESP8266 WiFi Module [part_number=ESP8266]
  Part2 = Breadboard Power Supply Board SMD
  R1 = Resistor [tolerance=±5% resistance=1k package=THT]
  R2 = Resistor [tolerance=±5% resistance=2k package=THT]
  ZS-042_RTC1 = ZS-042 RTC Module
  Part3 = Voltage Sensor 25V
  Part4 = Solar Cell
  Part5 = Solar Cell
  Part6 = Solar Cell
  R3 = Resistor [tolerance=±5% resistance=220 package="2010 [SMD]"]
  LED1 = LED - 5mm [color="Red (633nm)" package="5 mm [THT]"]

nets:
  N1: Part1.A0, Part3.S
  N2: Part1.A4/SDA, ZS-042_RTC1.SDA
  N3: Part1.A5/SCL, ZS-042_RTC1.SCL
  N4: Part1.D2, ESP8266.TXD
  N5: Part1.D3_PWM, R1.Pin_0
  5V: Part1.5V, ZS-042_RTC1.VCC
  GND: Part1.GND, ESP8266.GND, Part2.GND, R2.Pin_1, ZS-042_RTC1.GND, Part3.-
  N6: ESP8266.RXD, R1.Pin_1, R2.Pin_0
  VCC: ESP8266.VCC, ESP8266.RST, ESP8266.CH_PD, Part2.VCC
  N7: Part3.GND, Part6.-, LED1.cathode
  N8: Part3.VCC, Part3.+, Part4.+, R3.Pin_0
  N9: Part4.-, Part5.+
  N10: Part5.-, Part6.+
  N11: R3.Pin_1, LED1.anode

custom parts:
  ESP8266 WiFi Module: Generic WiFi Module based on the ESP8266 with onboard PCB antenna and UART communications
